# Fritzing sketch LED_Flame (saved by Fritzing 0.9.4)
breadboards: 1

parts:
  R1 = Resistor [tolerance=±5% resistance=220 package=THT]
  R2 = Resistor [tolerance=±5% resistance=220 package=THT]
  LED1 = LED - 5mm [color="Yellow (595nm)" package="5 mm [THT]"]
  LED2 = LED - 5mm [color="Yellow (595nm)" package="5 mm [THT]"]
  R3 = Resistor [tolerance=±5% resistance=220 package=THT]
  LED3 = LED - 5mm [color="Yellow (595nm)" package="5 mm [THT]"]
  R4 = Resistor [tolerance=±5% resistance=220 package=THT]
  LED4 = LED - 5mm [color="Yellow (595nm)" package="5 mm [THT]"]
  R5 = Resistor [tolerance=±5% resistance=220 package=THT]
  LED5 = LED - 5mm [color="Yellow (595nm)" package="5 mm [THT]"]
  Part1 = Arduino Uno (Rev3)

nets:
  N1: R1.Pin_0, LED1.cathode
  N2: R1.Pin_1, Part1.D11_PWM/MOSI
  N3: R2.Pin_0, LED2.cathode
  N4: R2.Pin_1, Part1.D10_PWM/SS
  N5: LED1.anode, LED2.anode, LED3.anode, LED4.anode, LED5.anode, Part1.GND
  N6: R3.Pin_0, LED3.cathode
  N7: R3.Pin_1, Part1.D9_PWM
  N8: R4.Pin_0, LED4.cathode
  N9: R4.Pin_1, Part1.D6_PWM
  N10: R5.Pin_0, LED5.cathode
  N11: R5.Pin_1, Part1.D5_PWM
